// Logisim project fulladder.circ as structural Verilog: 1 circuit, main circuit main
module main (
  input  A_0,
  input  A_1,
  input  A_2,
  input  B_0,
  input  B_1,
  input  B_2
);

  wire and_1_out, and_2_out, and_3_out, and_4_out, and_5_out, or_1_out, or_2_out, xor_1_out, xor_2_out,
       xor_3_out, xor_4_out, xor_5_out;

  xor xor_1 (xor_1_out, A_0, B_0);
  and and_1 (and_1_out, A_0, B_0);
  xor xor_2 (xor_2_out, A_1, B_1);
  and and_2 (and_2_out, A_1, B_1);
  or or_1 (or_1_out, and_2_out, and_4_out);
  xor xor_3 (xor_3_out, A_2, B_2);
  and and_3 (and_3_out, A_2, B_2);
  or or_2 (or_2_out, and_3_out, and_5_out);
  xor xor_4 (xor_4_out, and_1_out, xor_2_out);
  and and_4 (and_4_out, and_1_out, xor_2_out);
  xor xor_5 (xor_5_out, or_1_out, xor_3_out);
  and and_5 (and_5_out, or_1_out, xor_3_out);
  // Probe on xor_1_out
  // Probe on xor_4_out
  // Probe on xor_5_out
  // Probe on or_2_out

  // Notes on the sheet:
  //   First number
  //   Second number
  //   Полный сумматор (Full adder) двух 3-х битных входов
  //   Субханкулов Рустам Рамилевич Б01-108а subkhankulov.rr@phystech.edu
  //   C0
  //   C1
  //   C2
  //   Result bits
  //   S[0]
  //   S[1]
  //   S[2]
  //   C
  //   Carry bit
endmodule
